// Logisim project ep2.circ as structural Verilog: 16 circuits, main circuit main
module main (
  input  a7,
  input  a6,
  input  a5,
  input  a4,
  input  a3,
  input  a2,
  input  a1,
  input  a0,
  input  b7,
  input  b6,
  input  b5,
  input  b4,
  input  b3,
  input  b2,
  input  b1,
  input  b0,
  input  s2,
  input  s1,
  input  s0,
  output r7,
  output r6,
  output r5,
  output r4,
  output r3,
  output r2,
  output r1,
  output r0,
  output overflow
);

  wire comparator_1_eq, comparator_2_eq, comparator_3_eq, comparator_4_eq, \divisão_1_overflow ,
       \divisão_1_r0 , \divisão_1_r1 , \divisão_1_r2 , \divisão_1_r3 , \divisão_1_r4 , \divisão_1_r5 ,
       \divisão_1_r6 , \divisão_1_r7 , multiplexer_5_out, multiplexer_6_out, \multiplicação_1_overflow ,
       \multiplicação_1_r0 , \multiplicação_1_r1 , \multiplicação_1_r2 , \multiplicação_1_r3 ,
       \multiplicação_1_r4 , \multiplicação_1_r5 , \multiplicação_1_r6 , \multiplicação_1_r7 ,
       resto_1_out_17, resto_1_out_18, resto_1_out_19, resto_1_out_20, resto_1_out_21, resto_1_out_22,
       resto_1_out_23, resto_1_out_24, soma_total_1_overflow, soma_total_1_s0, soma_total_1_s1,
       soma_total_1_s2, soma_total_1_s3, soma_total_1_s4, soma_total_1_s5, soma_total_1_s6, soma_total_1_s7,
       \subtração_total_1_overflow , \subtração_total_1_r0 , \subtração_total_1_r1 , \subtração_total_1_r2 ,
       \subtração_total_1_r3 , \subtração_total_1_r4 , \subtração_total_1_r5 , \subtração_total_1_r6 ,
       \subtração_total_1_r7 ;
  wire [2:0] and_1_out, and_2_out, and_3_out, bit_extender_1_out, bit_extender_2_out, bit_extender_3_out,
       or_1_out;
  wire [7:0] converte_1_out_9, converte_2_out_9, converte_3_out_9, converte_4_out_9, converte_5_out_9,
       multiplexer_1_out, multiplexer_2_out, multiplexer_3_out, multiplexer_4_out;

  assign bit_extender_1_out = {{2{s2}}, s2};  // Bit_Extender bit_extender_1
  assign bit_extender_2_out = {{2{s1}}, s1};  // Bit_Extender bit_extender_2
  assign bit_extender_3_out = {{2{s0}}, s0};  // Bit_Extender bit_extender_3
  assign and_1_out = 3'b100 & bit_extender_1_out;  // AND_Gate and_1, 3 bits wide
  assign and_2_out = 3'b010 & bit_extender_2_out;  // AND_Gate and_2, 3 bits wide
  assign and_3_out = 3'b001 & bit_extender_3_out;  // AND_Gate and_3, 3 bits wide
  assign or_1_out = and_1_out | and_2_out | and_3_out;  // OR_Gate or_1, 3 bits wide
  Comparator #(.width(3), .mode("unsigned")) comparator_1 (
    .a(3'b001), .b(or_1_out), .eq(comparator_1_eq));  // open: gt, lt
  Comparator #(.width(3), .mode("unsigned")) comparator_2 (
    .a(3'b010), .b(or_1_out), .eq(comparator_2_eq));  // open: gt, lt
  Comparator #(.width(3), .mode("unsigned")) comparator_3 (
    .a(3'b011), .b(or_1_out), .eq(comparator_3_eq));  // open: gt, lt
  Comparator #(.width(3), .mode("unsigned")) comparator_4 (
    .a(3'b100), .b(or_1_out), .eq(comparator_4_eq));  // open: gt, lt
  Soma_total soma_total_1 (
    .a7(a7), .a6(a6), .a5(a5), .a4(a4), .a3(a3), .a2(a2), .a1(a1), .a0(a0), .b7(b7), .b6(b6), .b5(b5),
    .b4(b4), .b3(b3), .b2(b2), .b1(b1), .b0(b0), .s7(soma_total_1_s7), .s6(soma_total_1_s6),
    .s5(soma_total_1_s5), .s4(soma_total_1_s4), .s3(soma_total_1_s3), .s2(soma_total_1_s2),
    .s1(soma_total_1_s1), .s0(soma_total_1_s0), .overflow(soma_total_1_overflow));
  \Subtração_total  \subtração_total_1  (
    .a7(a7), .a6(a6), .a5(a5), .a4(a4), .a3(a3), .a2(a2), .a1(a1), .a0(a0), .b7(b7), .b6(b6), .b5(b5),
    .b4(b4), .b3(b3), .b2(b2), .b1(b1), .b0(b0), .r7(\subtração_total_1_r7 ), .r6(\subtração_total_1_r6 ),
    .r5(\subtração_total_1_r5 ), .r4(\subtração_total_1_r4 ), .r3(\subtração_total_1_r3 ),
    .r2(\subtração_total_1_r2 ), .r1(\subtração_total_1_r1 ), .r0(\subtração_total_1_r0 ),
    .overflow(\subtração_total_1_overflow ));
  \Multiplicação  \multiplicação_1  (
    .a7(a7), .a6(a6), .a5(a5), .a4(a4), .a3(a3), .a2(a2), .a1(a1), .a0(a0), .b7(b7), .b6(b6), .b5(b5),
    .b4(b4), .b3(b3), .b2(b2), .b1(b1), .b0(b0), .r7(\multiplicação_1_r7 ), .r6(\multiplicação_1_r6 ),
    .r5(\multiplicação_1_r5 ), .r4(\multiplicação_1_r4 ), .r3(\multiplicação_1_r3 ),
    .r2(\multiplicação_1_r2 ), .r1(\multiplicação_1_r1 ), .r0(\multiplicação_1_r0 ),
    .overflow(\multiplicação_1_overflow ));
  \Divisão  \divisão_1  (
    .a7(a7), .a6(a6), .a5(a5), .a4(a4), .a3(a3), .a2(a2), .a1(a1), .a0(a0), .b7(b7), .b6(b6), .b5(b5),
    .b4(b4), .b3(b3), .b2(b2), .b1(b1), .b0(b0), .r7(\divisão_1_r7 ), .r6(\divisão_1_r6 ),
    .r5(\divisão_1_r5 ), .r4(\divisão_1_r4 ), .r3(\divisão_1_r3 ), .r2(\divisão_1_r2 ), .r1(\divisão_1_r1 ),
    .r0(\divisão_1_r0 ), .overflow(\divisão_1_overflow ));  // open: out_25
  Resto resto_1 (
    .a7(a7), .a6(a6), .a5(a5), .a4(a4), .a3(a3), .a2(a2), .a1(a1), .a0(a0), .b7(b7), .b6(b6), .b5(b5),
    .b4(b4), .b3(b3), .b2(b2), .b1(b1), .b0(b0), .out_17(resto_1_out_17), .out_18(resto_1_out_18),
    .out_19(resto_1_out_19), .out_20(resto_1_out_20), .out_21(resto_1_out_21), .out_22(resto_1_out_22),
    .out_23(resto_1_out_23), .out_24(resto_1_out_24));
  Converte converte_1 (
    .n7(soma_total_1_s7), .n6(soma_total_1_s6), .n5(soma_total_1_s5), .n4(soma_total_1_s4),
    .n3(soma_total_1_s3), .n2(soma_total_1_s2), .n1(soma_total_1_s1), .n0(soma_total_1_s0),
    .out_9(converte_1_out_9));
  Converte converte_2 (
    .n7(\subtração_total_1_r7 ), .n6(\subtração_total_1_r6 ), .n5(\subtração_total_1_r5 ),
    .n4(\subtração_total_1_r4 ), .n3(\subtração_total_1_r3 ), .n2(\subtração_total_1_r2 ),
    .n1(\subtração_total_1_r1 ), .n0(\subtração_total_1_r0 ), .out_9(converte_2_out_9));
  Converte converte_3 (
    .n7(\multiplicação_1_r7 ), .n6(\multiplicação_1_r6 ), .n5(\multiplicação_1_r5 ),
    .n4(\multiplicação_1_r4 ), .n3(\multiplicação_1_r3 ), .n2(\multiplicação_1_r2 ),
    .n1(\multiplicação_1_r1 ), .n0(\multiplicação_1_r0 ), .out_9(converte_3_out_9));
  Converte converte_4 (
    .n7(\divisão_1_r7 ), .n6(\divisão_1_r6 ), .n5(\divisão_1_r5 ), .n4(\divisão_1_r4 ), .n3(\divisão_1_r3 ),
    .n2(\divisão_1_r2 ), .n1(\divisão_1_r1 ), .n0(\divisão_1_r0 ), .out_9(converte_4_out_9));
  Converte converte_5 (
    .n7(resto_1_out_17), .n6(resto_1_out_18), .n5(resto_1_out_19), .n4(resto_1_out_20), .n3(resto_1_out_21),
    .n2(resto_1_out_22), .n1(resto_1_out_23), .n0(resto_1_out_24), .out_9(converte_5_out_9));
  Multiplexer #(.width(8), .enable("false")) multiplexer_1 (
    .in0(converte_1_out_9), .in1(converte_2_out_9), .out(multiplexer_1_out), .sel(comparator_1_eq));
  Multiplexer #(.width(8), .enable("false")) multiplexer_2 (
    .in0(multiplexer_1_out), .in1(converte_3_out_9), .out(multiplexer_2_out), .sel(comparator_2_eq));
  Multiplexer #(.width(8), .enable("false")) multiplexer_3 (
    .in0(multiplexer_2_out), .in1(converte_4_out_9), .out(multiplexer_3_out), .sel(comparator_3_eq));
  Multiplexer #(.width(8), .enable("false")) multiplexer_4 (
    .in0(multiplexer_3_out), .in1(converte_5_out_9), .out(multiplexer_4_out), .sel(comparator_4_eq));
  Desconverte desconverte_1 (
    .in_1(multiplexer_4_out), .out_2(r7), .out_3(r6), .out_4(r5), .out_5(r4), .out_6(r3), .out_7(r2),
    .out_8(r1), .out_9(r0));
  Multiplexer #(.enable("false")) multiplexer_5 (
    .in0(soma_total_1_overflow), .in1(\subtração_total_1_overflow ), .out(multiplexer_5_out),
    .sel(comparator_1_eq));
  Multiplexer #(.enable("false")) multiplexer_6 (
    .in0(multiplexer_5_out), .in1(\multiplicação_1_overflow ), .out(multiplexer_6_out), .sel(comparator_2_eq));
  Multiplexer #(.enable("false")) multiplexer_7 (
    .in0(multiplexer_6_out), .in1(\divisão_1_overflow ), .out(overflow), .sel(comparator_3_eq));
endmodule

module Soma_de_bit (
  input  a,
  input  b,
  input  cin,
  output s,
  output cout
);

  wire and_1_out, and_2_out, xor_1_out;

  xor xor_1 (xor_1_out, a, b);
  xor xor_2 (s, xor_1_out, cin);
  and and_1 (and_1_out, xor_1_out, cin);
  and and_2 (and_2_out, a, b);
  or or_1 (cout, and_1_out, and_2_out);

  // Notes on the sheet:
  //   b: pull=down
  //   a: pull=down
  //   cin: pull=down
endmodule

module Soma_total (
  input  a7,
  input  a6,
  input  a5,
  input  a4,
  input  a3,
  input  a2,
  input  a1,
  input  a0,
  input  b7,
  input  b6,
  input  b5,
  input  b4,
  input  b3,
  input  b2,
  input  b1,
  input  b0,
  output s7,
  output s6,
  output s5,
  output s4,
  output s3,
  output s2,
  output s1,
  output s0,
  output overflow
);

  wire soma_de_bit_1_cout, soma_de_bit_2_cout, soma_de_bit_3_cout, soma_de_bit_4_cout, soma_de_bit_5_cout,
       soma_de_bit_6_cout, soma_de_bit_7_cout, xnor_1_out, xor_1_out;

  Soma_de_bit soma_de_bit_1 (.a(a0), .b(b0), .cin(1'b0), .s(s0), .cout(soma_de_bit_1_cout));
  Soma_de_bit soma_de_bit_2 (.a(a1), .b(b1), .cin(soma_de_bit_1_cout), .s(s1), .cout(soma_de_bit_2_cout));
  Soma_de_bit soma_de_bit_3 (.a(a2), .b(b2), .cin(soma_de_bit_2_cout), .s(s2), .cout(soma_de_bit_3_cout));
  Soma_de_bit soma_de_bit_4 (.a(a3), .b(b3), .cin(soma_de_bit_3_cout), .s(s3), .cout(soma_de_bit_4_cout));
  Soma_de_bit soma_de_bit_5 (.a(a4), .b(b4), .cin(soma_de_bit_4_cout), .s(s4), .cout(soma_de_bit_5_cout));
  Soma_de_bit soma_de_bit_6 (.a(a5), .b(b5), .cin(soma_de_bit_5_cout), .s(s5), .cout(soma_de_bit_6_cout));
  Soma_de_bit soma_de_bit_7 (.a(a6), .b(b6), .cin(soma_de_bit_6_cout), .s(s6), .cout(soma_de_bit_7_cout));
  Soma_de_bit soma_de_bit_8 (.a(a7), .b(b7), .cin(soma_de_bit_7_cout), .s(s7));  // open: cout
  xor xor_1 (xor_1_out, s7, a7);
  xnor xnor_1 (xnor_1_out, a7, b7);
  and and_1 (overflow, xor_1_out, xnor_1_out);
endmodule

module Muda_sinal (
  input  a7,
  input  a6,
  input  a5,
  input  a4,
  input  a3,
  input  a2,
  input  a1,
  input  a0,
  output r7,
  output r6,
  output r5,
  output r4,
  output r3,
  output r2,
  output r1,
  output r0
);

  wire not_1_out, not_2_out, not_3_out, not_4_out, not_5_out, not_6_out, not_7_out, not_8_out;

  not not_1 (not_1_out, a1);
  not not_2 (not_2_out, a0);
  not not_3 (not_3_out, a7);
  not not_4 (not_4_out, a6);
  not not_5 (not_5_out, a5);
  not not_6 (not_6_out, a4);
  not not_7 (not_7_out, a3);
  not not_8 (not_8_out, a2);
  Soma_total soma_total_1 (
    .a7(not_3_out), .a6(not_4_out), .a5(not_5_out), .a4(not_6_out), .a3(not_7_out), .a2(not_8_out),
    .a1(not_1_out), .a0(not_2_out), .b7(1'b0), .b6(1'b0), .b5(1'b0), .b4(1'b0), .b3(1'b0), .b2(1'b0),
    .b1(1'b0), .b0(1'b1), .s7(r7), .s6(r6), .s5(r5), .s4(r4), .s3(r3), .s2(r2), .s1(r1), .s0(r0));  // open: overflow
endmodule

module \Subtração_total  (
  input  a7,
  input  a6,
  input  a5,
  input  a4,
  input  a3,
  input  a2,
  input  a1,
  input  a0,
  input  b7,
  input  b6,
  input  b5,
  input  b4,
  input  b3,
  input  b2,
  input  b1,
  input  b0,
  output r7,
  output r6,
  output r5,
  output r4,
  output r3,
  output r2,
  output r1,
  output r0,
  output overflow
);

  wire muda_sinal_1_r0, muda_sinal_1_r1, muda_sinal_1_r2, muda_sinal_1_r3, muda_sinal_1_r4, muda_sinal_1_r5,
       muda_sinal_1_r6, muda_sinal_1_r7;

  Muda_sinal muda_sinal_1 (
    .a7(b7), .a6(b6), .a5(b5), .a4(b4), .a3(b3), .a2(b2), .a1(b1), .a0(b0), .r7(muda_sinal_1_r7),
    .r6(muda_sinal_1_r6), .r5(muda_sinal_1_r5), .r4(muda_sinal_1_r4), .r3(muda_sinal_1_r3),
    .r2(muda_sinal_1_r2), .r1(muda_sinal_1_r1), .r0(muda_sinal_1_r0));
  Soma_total soma_total_1 (
    .a7(a7), .a6(a6), .a5(a5), .a4(a4), .a3(a3), .a2(a2), .a1(a1), .a0(a0), .b7(muda_sinal_1_r7),
    .b6(muda_sinal_1_r6), .b5(muda_sinal_1_r5), .b4(muda_sinal_1_r4), .b3(muda_sinal_1_r3),
    .b2(muda_sinal_1_r2), .b1(muda_sinal_1_r1), .b0(muda_sinal_1_r0), .s7(r7), .s6(r6), .s5(r5), .s4(r4),
    .s3(r3), .s2(r2), .s1(r1), .s0(r0), .overflow(overflow));
endmodule

module \Multiplicação  (
  input  a7,
  input  a6,
  input  a5,
  input  a4,
  input  a3,
  input  a2,
  input  a1,
  input  a0,
  input  b7,
  input  b6,
  input  b5,
  input  b4,
  input  b3,
  input  b2,
  input  b1,
  input  b0,
  output r7,
  output r6,
  output r5,
  output r4,
  output r3,
  output r2,
  output r1,
  output r0,
  output overflow
);

  wire comparator_1_eq, not_1_out, xor_1_out, xor_2_out;
  wire [7:0] converte_1_out_9, deslocador_1_out_3, deslocador_2_out_3, deslocador_3_out_3,
       deslocador_4_out_3, deslocador_5_out_3, deslocador_6_out_3, deslocador_7_out_3,
       soma_convertido_1_out_3, soma_convertido_2_out_3, soma_convertido_3_out_3, soma_convertido_4_out_3,
       soma_convertido_5_out_3, soma_convertido_6_out_3, soma_convertido_7_out_3, soma_convertido_8_out_3,
       verifica_bit_1_out_3, verifica_bit_2_out_3, verifica_bit_3_out_3, verifica_bit_4_out_3,
       verifica_bit_5_out_3, verifica_bit_6_out_3, verifica_bit_7_out_3, verifica_bit_8_out_3;

  Converte converte_1 (
    .n7(a7), .n6(a6), .n5(a5), .n4(a4), .n3(a3), .n2(a2), .n1(a1), .n0(a0), .out_9(converte_1_out_9));
  Verifica_bit verifica_bit_1 (.in_1(converte_1_out_9), .in_2(b7), .out_3(verifica_bit_1_out_3));
  Verifica_bit verifica_bit_2 (.in_1(converte_1_out_9), .in_2(b6), .out_3(verifica_bit_2_out_3));
  Verifica_bit verifica_bit_3 (.in_1(converte_1_out_9), .in_2(b5), .out_3(verifica_bit_3_out_3));
  Verifica_bit verifica_bit_4 (.in_1(converte_1_out_9), .in_2(b4), .out_3(verifica_bit_4_out_3));
  Verifica_bit verifica_bit_5 (.in_1(converte_1_out_9), .in_2(b3), .out_3(verifica_bit_5_out_3));
  Verifica_bit verifica_bit_6 (.in_1(converte_1_out_9), .in_2(b2), .out_3(verifica_bit_6_out_3));
  Verifica_bit verifica_bit_7 (.in_1(converte_1_out_9), .in_2(b1), .out_3(verifica_bit_7_out_3));
  Verifica_bit verifica_bit_8 (.in_1(converte_1_out_9), .in_2(b0), .out_3(verifica_bit_8_out_3));
  Deslocador deslocador_1 (.in_1(verifica_bit_1_out_3), .in_2(3'b111), .out_3(deslocador_1_out_3));
  Deslocador deslocador_2 (.in_1(verifica_bit_2_out_3), .in_2(3'b110), .out_3(deslocador_2_out_3));
  Deslocador deslocador_3 (.in_1(verifica_bit_3_out_3), .in_2(3'b101), .out_3(deslocador_3_out_3));
  Deslocador deslocador_4 (.in_1(verifica_bit_4_out_3), .in_2(3'b100), .out_3(deslocador_4_out_3));
  Deslocador deslocador_5 (.in_1(verifica_bit_5_out_3), .in_2(3'b011), .out_3(deslocador_5_out_3));
  Deslocador deslocador_6 (.in_1(verifica_bit_6_out_3), .in_2(3'b010), .out_3(deslocador_6_out_3));
  Deslocador deslocador_7 (.in_1(verifica_bit_7_out_3), .in_2(3'b001), .out_3(deslocador_7_out_3));
  Soma_convertido soma_convertido_1 (
    .in_1(deslocador_1_out_3), .in_2(soma_convertido_2_out_3), .out_3(soma_convertido_1_out_3));  // open: overflow
  Soma_convertido soma_convertido_2 (
    .in_1(deslocador_2_out_3), .in_2(soma_convertido_3_out_3), .out_3(soma_convertido_2_out_3));  // open: overflow
  Soma_convertido soma_convertido_3 (
    .in_1(deslocador_3_out_3), .in_2(soma_convertido_4_out_3), .out_3(soma_convertido_3_out_3));  // open: overflow
  Soma_convertido soma_convertido_4 (
    .in_1(deslocador_4_out_3), .in_2(soma_convertido_5_out_3), .out_3(soma_convertido_4_out_3));  // open: overflow
  Soma_convertido soma_convertido_5 (
    .in_1(deslocador_5_out_3), .in_2(soma_convertido_6_out_3), .out_3(soma_convertido_5_out_3));  // open: overflow
  Soma_convertido soma_convertido_6 (
    .in_1(deslocador_6_out_3), .in_2(soma_convertido_7_out_3), .out_3(soma_convertido_6_out_3));  // open: overflow
  Soma_convertido soma_convertido_7 (
    .in_1(deslocador_7_out_3), .in_2(soma_convertido_8_out_3), .out_3(soma_convertido_7_out_3));  // open: overflow
  Soma_convertido soma_convertido_8 (
    .in_1(verifica_bit_8_out_3), .in_2({8{1'b0}}), .out_3(soma_convertido_8_out_3));  // open: overflow
  Desconverte desconverte_1 (
    .in_1(soma_convertido_1_out_3), .out_2(r7), .out_3(r6), .out_4(r5), .out_5(r4), .out_6(r3), .out_7(r2),
    .out_8(r1), .out_9(r0));
  xor xor_1 (xor_1_out, a7, b7);
  Comparator comparator_1 (.a(soma_convertido_1_out_3), .b({8{1'b0}}), .eq(comparator_1_eq));  // open: gt, lt
  xor xor_2 (xor_2_out, r7, xor_1_out);
  not not_1 (not_1_out, comparator_1_eq);
  and and_1 (overflow, xor_2_out, not_1_out);
endmodule

module Verifica_bit (
  input  [7:0] in_1,
  input  in_2,
  output [7:0] out_3
);

  Multiplexer #(.width(8), .enable("false")) multiplexer_1 (.in0({8{1'b0}}), .in1(in_1), .out(out_3), .sel(in_2));
endmodule

module Deslocador (
  input  [7:0] in_1,
  input  [2:0] in_2,
  output [7:0] out_3
);

  Shifter shifter_1 (.in(in_1), .\dist (in_2), .out(out_3));
endmodule

module Converte (
  input  n7,
  input  n6,
  input  n5,
  input  n4,
  input  n3,
  input  n2,
  input  n1,
  input  n0,
  output [7:0] out_9
);

  wire [7:0] and_1_out, and_2_out, and_3_out, and_4_out, and_5_out, and_6_out, and_7_out, and_8_out,
       bit_extender_1_out, bit_extender_2_out, bit_extender_3_out, bit_extender_4_out, bit_extender_5_out,
       bit_extender_6_out, bit_extender_7_out, bit_extender_8_out;

  assign bit_extender_1_out = {{7{n7}}, n7};  // Bit_Extender bit_extender_1
  assign bit_extender_2_out = {{7{n6}}, n6};  // Bit_Extender bit_extender_2
  assign bit_extender_3_out = {{7{n5}}, n5};  // Bit_Extender bit_extender_3
  assign bit_extender_4_out = {{7{n4}}, n4};  // Bit_Extender bit_extender_4
  assign bit_extender_5_out = {{7{n3}}, n3};  // Bit_Extender bit_extender_5
  assign bit_extender_6_out = {{7{n2}}, n2};  // Bit_Extender bit_extender_6
  assign bit_extender_7_out = {{7{n1}}, n1};  // Bit_Extender bit_extender_7
  assign bit_extender_8_out = {{7{n0}}, n0};  // Bit_Extender bit_extender_8
  assign and_1_out = 8'h80 & bit_extender_1_out;  // AND_Gate and_1, 8 bits wide
  assign and_2_out = 8'h40 & bit_extender_2_out;  // AND_Gate and_2, 8 bits wide
  assign and_3_out = 8'h20 & bit_extender_3_out;  // AND_Gate and_3, 8 bits wide
  assign and_4_out = 8'h10 & bit_extender_4_out;  // AND_Gate and_4, 8 bits wide
  assign and_5_out = 8'h8 & bit_extender_5_out;  // AND_Gate and_5, 8 bits wide
  assign and_6_out = 8'h4 & bit_extender_6_out;  // AND_Gate and_6, 8 bits wide
  assign and_7_out = 8'h2 & bit_extender_7_out;  // AND_Gate and_7, 8 bits wide
  assign and_8_out = 8'h1 & bit_extender_8_out;  // AND_Gate and_8, 8 bits wide
  assign out_9 = and_1_out | and_2_out | and_3_out | and_4_out | and_5_out | and_6_out | and_7_out | and_8_out;  // OR_Gate or_1, 8 bits wide
endmodule

module Desconverte (
  input  [7:0] in_1,
  output out_2,
  output out_3,
  output out_4,
  output out_5,
  output out_6,
  output out_7,
  output out_8,
  output out_9
);

  wire [7:0] and_1_out, and_2_out, and_3_out, and_4_out, and_5_out, and_6_out, and_7_out, and_8_out;

  assign and_1_out = 8'h80 & in_1;  // AND_Gate and_1, 8 bits wide
  assign and_2_out = 8'h40 & in_1;  // AND_Gate and_2, 8 bits wide
  assign and_3_out = 8'h20 & in_1;  // AND_Gate and_3, 8 bits wide
  assign and_4_out = 8'h10 & in_1;  // AND_Gate and_4, 8 bits wide
  assign and_5_out = 8'h8 & in_1;  // AND_Gate and_5, 8 bits wide
  assign and_6_out = 8'h4 & in_1;  // AND_Gate and_6, 8 bits wide
  assign and_7_out = 8'h2 & in_1;  // AND_Gate and_7, 8 bits wide
  assign and_8_out = 8'h1 & in_1;  // AND_Gate and_8, 8 bits wide
  Comparator comparator_1 (.a(and_1_out), .b({8{1'b0}}), .lt(out_2));  // open: gt, eq
  Comparator comparator_2 (.a(and_2_out), .b({8{1'b0}}), .gt(out_3));  // open: eq, lt
  Comparator comparator_3 (.a(and_3_out), .b({8{1'b0}}), .gt(out_4));  // open: eq, lt
  Comparator comparator_4 (.a(and_4_out), .b({8{1'b0}}), .gt(out_5));  // open: eq, lt
  Comparator comparator_5 (.a(and_5_out), .b({8{1'b0}}), .gt(out_6));  // open: eq, lt
  Comparator comparator_6 (.a(and_6_out), .b({8{1'b0}}), .gt(out_7));  // open: eq, lt
  Comparator comparator_7 (.a(and_7_out), .b({8{1'b0}}), .gt(out_8));  // open: eq, lt
  Comparator comparator_8 (.a(and_8_out), .b({8{1'b0}}), .gt(out_9));  // open: eq, lt

  // Notes on the sheet:
  //   in_1: pull=down
endmodule

module Soma_convertido (
  input  [7:0] in_1,
  input  [7:0] in_2,
  output [7:0] out_3,
  output overflow
);

  wire desconverte_1_out_2, desconverte_1_out_3, desconverte_1_out_4, desconverte_1_out_5,
       desconverte_1_out_6, desconverte_1_out_7, desconverte_1_out_8, desconverte_1_out_9,
       desconverte_2_out_2, desconverte_2_out_3, desconverte_2_out_4, desconverte_2_out_5,
       desconverte_2_out_6, desconverte_2_out_7, desconverte_2_out_8, desconverte_2_out_9, soma_total_1_s0,
       soma_total_1_s1, soma_total_1_s2, soma_total_1_s3, soma_total_1_s4, soma_total_1_s5, soma_total_1_s6,
       soma_total_1_s7;

  Desconverte desconverte_1 (
    .in_1(in_1), .out_2(desconverte_1_out_2), .out_3(desconverte_1_out_3), .out_4(desconverte_1_out_4),
    .out_5(desconverte_1_out_5), .out_6(desconverte_1_out_6), .out_7(desconverte_1_out_7),
    .out_8(desconverte_1_out_8), .out_9(desconverte_1_out_9));
  Desconverte desconverte_2 (
    .in_1(in_2), .out_2(desconverte_2_out_2), .out_3(desconverte_2_out_3), .out_4(desconverte_2_out_4),
    .out_5(desconverte_2_out_5), .out_6(desconverte_2_out_6), .out_7(desconverte_2_out_7),
    .out_8(desconverte_2_out_8), .out_9(desconverte_2_out_9));
  Soma_total soma_total_1 (
    .a7(desconverte_1_out_2), .a6(desconverte_1_out_3), .a5(desconverte_1_out_4), .a4(desconverte_1_out_5),
    .a3(desconverte_1_out_6), .a2(desconverte_1_out_7), .a1(desconverte_1_out_8), .a0(desconverte_1_out_9),
    .b7(desconverte_2_out_2), .b6(desconverte_2_out_3), .b5(desconverte_2_out_4), .b4(desconverte_2_out_5),
    .b3(desconverte_2_out_6), .b2(desconverte_2_out_7), .b1(desconverte_2_out_8), .b0(desconverte_2_out_9),
    .s7(soma_total_1_s7), .s6(soma_total_1_s6), .s5(soma_total_1_s5), .s4(soma_total_1_s4),
    .s3(soma_total_1_s3), .s2(soma_total_1_s2), .s1(soma_total_1_s1), .s0(soma_total_1_s0),
    .overflow(overflow));
  Converte converte_1 (
    .n7(soma_total_1_s7), .n6(soma_total_1_s6), .n5(soma_total_1_s5), .n4(soma_total_1_s4),
    .n3(soma_total_1_s3), .n2(soma_total_1_s2), .n1(soma_total_1_s1), .n0(soma_total_1_s0), .out_9(out_3));
endmodule

module Subtrai_convertido (
  input  [7:0] in_1,
  input  [7:0] in_2,
  output [7:0] out_3,
  output overflow
);

  wire desconverte_1_out_2, desconverte_1_out_3, desconverte_1_out_4, desconverte_1_out_5,
       desconverte_1_out_6, desconverte_1_out_7, desconverte_1_out_8, desconverte_1_out_9,
       desconverte_2_out_2, desconverte_2_out_3, desconverte_2_out_4, desconverte_2_out_5,
       desconverte_2_out_6, desconverte_2_out_7, desconverte_2_out_8, desconverte_2_out_9,
       \subtração_total_1_r0 , \subtração_total_1_r1 , \subtração_total_1_r2 , \subtração_total_1_r3 ,
       \subtração_total_1_r4 , \subtração_total_1_r5 , \subtração_total_1_r6 , \subtração_total_1_r7 ;

  Desconverte desconverte_1 (
    .in_1(in_1), .out_2(desconverte_1_out_2), .out_3(desconverte_1_out_3), .out_4(desconverte_1_out_4),
    .out_5(desconverte_1_out_5), .out_6(desconverte_1_out_6), .out_7(desconverte_1_out_7),
    .out_8(desconverte_1_out_8), .out_9(desconverte_1_out_9));
  Desconverte desconverte_2 (
    .in_1(in_2), .out_2(desconverte_2_out_2), .out_3(desconverte_2_out_3), .out_4(desconverte_2_out_4),
    .out_5(desconverte_2_out_5), .out_6(desconverte_2_out_6), .out_7(desconverte_2_out_7),
    .out_8(desconverte_2_out_8), .out_9(desconverte_2_out_9));
  \Subtração_total  \subtração_total_1  (
    .a7(desconverte_1_out_2), .a6(desconverte_1_out_3), .a5(desconverte_1_out_4), .a4(desconverte_1_out_5),
    .a3(desconverte_1_out_6), .a2(desconverte_1_out_7), .a1(desconverte_1_out_8), .a0(desconverte_1_out_9),
    .b7(desconverte_2_out_2), .b6(desconverte_2_out_3), .b5(desconverte_2_out_4), .b4(desconverte_2_out_5),
    .b3(desconverte_2_out_6), .b2(desconverte_2_out_7), .b1(desconverte_2_out_8), .b0(desconverte_2_out_9),
    .r7(\subtração_total_1_r7 ), .r6(\subtração_total_1_r6 ), .r5(\subtração_total_1_r5 ),
    .r4(\subtração_total_1_r4 ), .r3(\subtração_total_1_r3 ), .r2(\subtração_total_1_r2 ),
    .r1(\subtração_total_1_r1 ), .r0(\subtração_total_1_r0 ), .overflow(overflow));
  Converte converte_1 (
    .n7(\subtração_total_1_r7 ), .n6(\subtração_total_1_r6 ), .n5(\subtração_total_1_r5 ),
    .n4(\subtração_total_1_r4 ), .n3(\subtração_total_1_r3 ), .n2(\subtração_total_1_r2 ),
    .n1(\subtração_total_1_r1 ), .n0(\subtração_total_1_r0 ), .out_9(out_3));
endmodule

module \Divisão  (
  input  a7,
  input  a6,
  input  a5,
  input  a4,
  input  a3,
  input  a2,
  input  a1,
  input  a0,
  input  b7,
  input  b6,
  input  b5,
  input  b4,
  input  b3,
  input  b2,
  input  b1,
  input  b0,
  output r7,
  output r6,
  output r5,
  output r4,
  output r3,
  output r2,
  output r1,
  output r0,
  output [7:0] out_25,
  output overflow
);

  wire desconverte_1_out_2, desconverte_1_out_3, desconverte_1_out_4, desconverte_1_out_5,
       desconverte_1_out_6, desconverte_1_out_7, desconverte_1_out_8, desconverte_1_out_9, divisor_1_s0,
       divisor_1_s1, divisor_1_s2, divisor_1_s3, divisor_1_s4, divisor_1_s5, divisor_1_s6, divisor_1_s7,
       muda_sinal_1_r0, muda_sinal_1_r1, muda_sinal_1_r2, muda_sinal_1_r3, muda_sinal_1_r4, muda_sinal_1_r5,
       muda_sinal_1_r6, muda_sinal_1_r7, muda_sinal_2_r0, muda_sinal_2_r1, muda_sinal_2_r2, muda_sinal_2_r3,
       muda_sinal_2_r4, muda_sinal_2_r5, muda_sinal_2_r6, muda_sinal_2_r7, muda_sinal_3_r0, muda_sinal_3_r1,
       muda_sinal_3_r2, muda_sinal_3_r3, muda_sinal_3_r4, muda_sinal_3_r5, muda_sinal_3_r6, muda_sinal_3_r7,
       xor_1_out;
  wire [7:0] converte_1_out_9, converte_2_out_9, converte_3_out_9, converte_4_out_9, converte_5_out_9,
       converte_6_out_9, multiplexer_1_out, multiplexer_2_out, multiplexer_3_out;

  Muda_sinal muda_sinal_1 (
    .a7(a7), .a6(a6), .a5(a5), .a4(a4), .a3(a3), .a2(a2), .a1(a1), .a0(a0), .r7(muda_sinal_1_r7),
    .r6(muda_sinal_1_r6), .r5(muda_sinal_1_r5), .r4(muda_sinal_1_r4), .r3(muda_sinal_1_r3),
    .r2(muda_sinal_1_r2), .r1(muda_sinal_1_r1), .r0(muda_sinal_1_r0));
  Muda_sinal muda_sinal_2 (
    .a7(b7), .a6(b6), .a5(b5), .a4(b4), .a3(b3), .a2(b2), .a1(b1), .a0(b0), .r7(muda_sinal_2_r7),
    .r6(muda_sinal_2_r6), .r5(muda_sinal_2_r5), .r4(muda_sinal_2_r4), .r3(muda_sinal_2_r3),
    .r2(muda_sinal_2_r2), .r1(muda_sinal_2_r1), .r0(muda_sinal_2_r0));
  Converte converte_1 (
    .n7(a7), .n6(a6), .n5(a5), .n4(a4), .n3(a3), .n2(a2), .n1(a1), .n0(a0), .out_9(converte_1_out_9));
  Converte converte_2 (
    .n7(muda_sinal_1_r7), .n6(muda_sinal_1_r6), .n5(muda_sinal_1_r5), .n4(muda_sinal_1_r4),
    .n3(muda_sinal_1_r3), .n2(muda_sinal_1_r2), .n1(muda_sinal_1_r1), .n0(muda_sinal_1_r0),
    .out_9(converte_2_out_9));
  Converte converte_3 (
    .n7(b7), .n6(b6), .n5(b5), .n4(b4), .n3(b3), .n2(b2), .n1(b1), .n0(b0), .out_9(converte_3_out_9));
  Converte converte_4 (
    .n7(muda_sinal_2_r7), .n6(muda_sinal_2_r6), .n5(muda_sinal_2_r5), .n4(muda_sinal_2_r4),
    .n3(muda_sinal_2_r3), .n2(muda_sinal_2_r2), .n1(muda_sinal_2_r1), .n0(muda_sinal_2_r0),
    .out_9(converte_4_out_9));
  Multiplexer #(.width(8), .enable("false")) multiplexer_1 (
    .in0(converte_1_out_9), .in1(converte_2_out_9), .out(multiplexer_1_out), .sel(a7));
  Multiplexer #(.width(8), .enable("false")) multiplexer_2 (
    .in0(converte_3_out_9), .in1(converte_4_out_9), .out(multiplexer_2_out), .sel(b7));
  Desconverte desconverte_1 (
    .in_1(multiplexer_1_out), .out_2(desconverte_1_out_2), .out_3(desconverte_1_out_3),
    .out_4(desconverte_1_out_4), .out_5(desconverte_1_out_5), .out_6(desconverte_1_out_6),
    .out_7(desconverte_1_out_7), .out_8(desconverte_1_out_8), .out_9(desconverte_1_out_9));
  Comparator comparator_1 (.a({8{1'b0}}), .b(multiplexer_2_out), .eq(overflow));  // open: gt, lt
  xor xor_1 (xor_1_out, a7, b7);
  Divisor divisor_1 (
    .a7(desconverte_1_out_2), .a6(desconverte_1_out_3), .a5(desconverte_1_out_4), .a4(desconverte_1_out_5),
    .a3(desconverte_1_out_6), .a2(desconverte_1_out_7), .a1(desconverte_1_out_8), .a0(desconverte_1_out_9),
    .in_9(multiplexer_2_out), .s7(divisor_1_s7), .s6(divisor_1_s6), .s5(divisor_1_s5), .s4(divisor_1_s4),
    .s3(divisor_1_s3), .s2(divisor_1_s2), .s1(divisor_1_s1), .s0(divisor_1_s0), .out_18(out_25));
  Converte converte_5 (
    .n7(divisor_1_s7), .n6(divisor_1_s6), .n5(divisor_1_s5), .n4(divisor_1_s4), .n3(divisor_1_s3),
    .n2(divisor_1_s2), .n1(divisor_1_s1), .n0(divisor_1_s0), .out_9(converte_5_out_9));
  Muda_sinal muda_sinal_3 (
    .a7(divisor_1_s7), .a6(divisor_1_s6), .a5(divisor_1_s5), .a4(divisor_1_s4), .a3(divisor_1_s3),
    .a2(divisor_1_s2), .a1(divisor_1_s1), .a0(divisor_1_s0), .r7(muda_sinal_3_r7), .r6(muda_sinal_3_r6),
    .r5(muda_sinal_3_r5), .r4(muda_sinal_3_r4), .r3(muda_sinal_3_r3), .r2(muda_sinal_3_r2),
    .r1(muda_sinal_3_r1), .r0(muda_sinal_3_r0));
  Converte converte_6 (
    .n7(muda_sinal_3_r7), .n6(muda_sinal_3_r6), .n5(muda_sinal_3_r5), .n4(muda_sinal_3_r4),
    .n3(muda_sinal_3_r3), .n2(muda_sinal_3_r2), .n1(muda_sinal_3_r1), .n0(muda_sinal_3_r0),
    .out_9(converte_6_out_9));
  Multiplexer #(.width(8), .enable("false")) multiplexer_3 (
    .in0(converte_5_out_9), .in1(converte_6_out_9), .out(multiplexer_3_out), .sel(xor_1_out));
  Desconverte desconverte_2 (
    .in_1(multiplexer_3_out), .out_2(r7), .out_3(r6), .out_4(r5), .out_5(r4), .out_6(r3), .out_7(r2),
    .out_8(r1), .out_9(r0));
endmodule

module Divisor (
  input  a7,
  input  a6,
  input  a5,
  input  a4,
  input  a3,
  input  a2,
  input  a1,
  input  a0,
  input  [7:0] in_9,
  output s7,
  output s6,
  output s5,
  output s4,
  output s3,
  output s2,
  output s1,
  output s0,
  output [7:0] out_18
);

  wire [7:0] converte_1_out_9, deslocador_1_out_3, multiplexer_1_out, processo_interno_divisor_1_out_5,
       processo_interno_divisor_2_out_5, processo_interno_divisor_3_out_5, processo_interno_divisor_4_out_5,
       processo_interno_divisor_5_out_5, processo_interno_divisor_6_out_5, subtrai_convertido_1_out_3;

  Converte converte_1 (
    .n7(1'b0), .n6(1'b0), .n5(1'b0), .n4(1'b0), .n3(1'b0), .n2(1'b0), .n1(1'b0), .n0(a6),
    .out_9(converte_1_out_9));
  Subtrai_convertido subtrai_convertido_1 (
    .in_1(converte_1_out_9), .in_2(multiplexer_1_out), .out_3(subtrai_convertido_1_out_3));  // open: overflow
  Comparator comparator_1 (.a(in_9), .b(converte_1_out_9), .lt(s6));  // open: gt, eq
  Multiplexer #(.width(8), .enable("false")) multiplexer_1 (
    .in0({8{1'b0}}), .in1(in_9), .out(multiplexer_1_out), .sel(s6));
  Deslocador deslocador_1 (.in_1(subtrai_convertido_1_out_3), .in_2(3'b001), .out_3(deslocador_1_out_3));
  Processo_Interno_Divisor processo_interno_divisor_1 (
    .b(in_9), .Resto_deslocado(deslocador_1_out_3), .in_3(a5), .out_4(s5),
    .out_5(processo_interno_divisor_1_out_5));
  Processo_Interno_Divisor processo_interno_divisor_2 (
    .b(in_9), .Resto_deslocado(processo_interno_divisor_1_out_5), .in_3(a4), .out_4(s4),
    .out_5(processo_interno_divisor_2_out_5));
  Processo_Interno_Divisor processo_interno_divisor_3 (
    .b(in_9), .Resto_deslocado(processo_interno_divisor_2_out_5), .in_3(a3), .out_4(s3),
    .out_5(processo_interno_divisor_3_out_5));
  Processo_Interno_Divisor processo_interno_divisor_4 (
    .b(in_9), .Resto_deslocado(processo_interno_divisor_3_out_5), .in_3(a2), .out_4(s2),
    .out_5(processo_interno_divisor_4_out_5));
  Processo_Interno_Divisor processo_interno_divisor_5 (
    .b(in_9), .Resto_deslocado(processo_interno_divisor_4_out_5), .in_3(a1), .out_4(s1),
    .out_5(processo_interno_divisor_5_out_5));
  Processo_Interno_Divisor processo_interno_divisor_6 (
    .b(in_9), .Resto_deslocado(processo_interno_divisor_5_out_5), .in_3(a0), .out_4(s0),
    .out_5(processo_interno_divisor_6_out_5));
  Shifter #(.shift("lr")) shifter_1 (.in(processo_interno_divisor_6_out_5), .\dist (3'b001), .out(out_18));

  assign s7 = a7;
endmodule

// PID
module Processo_Interno_Divisor (
  input  [7:0] b,
  input  [7:0] Resto_deslocado,
  input  in_3,
  output out_4,
  output [7:0] out_5
);

  wire comparator_1_eq, comparator_1_lt;
  wire [7:0] converte_1_out_9, multiplexer_1_out, soma_convertido_1_out_3, subtrai_convertido_1_out_3;

  Converte converte_1 (
    .n7(1'b0), .n6(1'b0), .n5(1'b0), .n4(1'b0), .n3(1'b0), .n2(1'b0), .n1(1'b0), .n0(in_3),
    .out_9(converte_1_out_9));
  Soma_convertido soma_convertido_1 (
    .in_1(Resto_deslocado), .in_2(converte_1_out_9), .out_3(soma_convertido_1_out_3));  // open: overflow
  Comparator comparator_1 (.a(b), .b(soma_convertido_1_out_3), .eq(comparator_1_eq), .lt(comparator_1_lt));  // open: gt
  or or_1 (out_4, comparator_1_eq, comparator_1_lt);
  Multiplexer #(.width(8), .enable("false")) multiplexer_1 (
    .in0({8{1'b0}}), .in1(b), .out(multiplexer_1_out), .sel(out_4));
  Subtrai_convertido subtrai_convertido_1 (
    .in_1(soma_convertido_1_out_3), .in_2(multiplexer_1_out), .out_3(subtrai_convertido_1_out_3));  // open: overflow
  Deslocador deslocador_1 (.in_1(subtrai_convertido_1_out_3), .in_2(3'b001), .out_3(out_5));
endmodule

module Resto (
  input  a7,
  input  a6,
  input  a5,
  input  a4,
  input  a3,
  input  a2,
  input  a1,
  input  a0,
  input  b7,
  input  b6,
  input  b5,
  input  b4,
  input  b3,
  input  b2,
  input  b1,
  input  b0,
  output out_17,
  output out_18,
  output out_19,
  output out_20,
  output out_21,
  output out_22,
  output out_23,
  output out_24
);

  wire [7:0] \divisão_1_out_25 ;

  \Divisão  \divisão_1  (
    .a7(a7), .a6(a6), .a5(a5), .a4(a4), .a3(a3), .a2(a2), .a1(a1), .a0(a0), .b7(b7), .b6(b6), .b5(b5),
    .b4(b4), .b3(b3), .b2(b2), .b1(b1), .b0(b0), .out_25(\divisão_1_out_25 ));  // open: r7, r6, r5, r4, r3, r2, r1, r0, overflow
  Desconverte desconverte_1 (
    .in_1(\divisão_1_out_25 ), .out_2(out_17), .out_3(out_18), .out_4(out_19), .out_5(out_20),
    .out_6(out_21), .out_7(out_22), .out_8(out_23), .out_9(out_24));
endmodule
