// Logisim project EP4.circ as structural Verilog
module ALU1 (
  input  [15:0] Entrada_1,
  input  [15:0] Entrada_2,
  input  [15:0] Resultado
);

  Soma Soma ();  // open: Entrada_1, Entrada_2, Res_Soma, Overflow
endmodule

module ALU (
);

  wire clock_1_out, CTRL_ctrlacc, CTRL_ctrljmp, CTRL_ctrlram, CTRL_ctrlstp, CTRL_ctrlstr;
  wire [7:0] IR_instruction, IR_parameter, IR_parameter_2, PC_out_5;
  wire [15:0] ACC_q, demultiplexer_1_out0, demultiplexer_1_out1, \RAM_saída_ram ;

  Clock clock_1 (.out(clock_1_out));
  PC PC (.STP(CTRL_ctrlstp), .JMPAdress(IR_parameter_2), .JMP(CTRL_ctrljmp), .out_5(PC_out_5), .Clock(clock_1_out));
  RAM RAM (
    .in_1(IR_parameter), .in_2(PC_out_5), .CtrlRam(CTRL_ctrlram), .in_3(ACC_q), .CtrlStr(CTRL_ctrlstr),
    .Clock(clock_1_out), .\Saída_RAM (\RAM_saída_ram ));
  Demultiplexer #(.width(16), .enable("false")) demultiplexer_1 (
    .out0(demultiplexer_1_out0), .out1(demultiplexer_1_out1), .in(\RAM_saída_ram ), .sel(clock_1_out));
  CTRL CTRL (
    .Instruction(IR_instruction), .Clock(clock_1_out), .CtrlRam(CTRL_ctrlram), .CtrlStr(CTRL_ctrlstr),
    .CtrlAcc(CTRL_ctrlacc), .CtrlJmp(CTRL_ctrljmp), .CtrlStp(CTRL_ctrlstp));
  IR IR (
    .in_1(demultiplexer_1_out1), .Clock(clock_1_out), .Parameter(IR_parameter), .Parameter_2(IR_parameter_2),
    .Instruction(IR_instruction));
  Register #(.width(16), .trigger("low")) ACC (
    .D(demultiplexer_1_out0), .en(CTRL_ctrlacc), .Q(ACC_q), .clk(clock_1_out));  // open: clr

  // Notes on the sheet:
  //   Barramento do Clock
  //   Barramento de Controle
  //   Barramento de Dados
  //   Barramento de Endereço
endmodule

module Soma (
  input  [15:0] Entrada_1,
  input  [15:0] Entrada_2,
  output [15:0] Res_Soma,
  output Overflow
);

  Adder #(.width(16)) adder_1 (.a(Entrada_1), .b(Entrada_2), .out(Res_Soma), .cout(Overflow));  // open: cin
endmodule

module \Subtração  (
  input  [15:0] Minuendo,
  input  [15:0] SUbtraendo,
  output [15:0] \Res_Subtração 
);

  Subtractor #(.width(16)) subtractor_1 (.a(Minuendo), .b(SUbtraendo), .out(\Res_Subtração ));  // open: bin, bout
endmodule

module \Multiplicação  (
  input  [15:0] Entrada_1,
  input  [15:0] Entrada_2,
  output [15:0] \Res_Multiplicação 
);

  Multiplier #(.width(16)) multiplier_1 (.a(Entrada_1), .b(Entrada_2), .out(\Res_Multiplicação ));  // open: cin, cout
endmodule

module \Divisão  (
  input  [15:0] Dividendo,
  input  [15:0] Divisor,
  output [15:0] Quociente,
  output [15:0] Resto
);

  Divider #(.width(16)) divider_1 (.a(Dividendo), .b(Divisor), .out(Quociente), .rem(Resto));  // open: upper
endmodule

module PC (
  input  STP,
  input  [7:0] JMPAdress,
  input  JMP,
  input  Clock,
  output [7:0] out_5
);

  wire and_1_out, controlled_buffer_1_out, n0_qn, n1_qn, n2_qn, n3_qn, n4_qn, n5_qn, n6_qn, not_1_out,
       not_2_out, not_3_out, not_4_out, not_5_out, not_6_out, not_7_out, not_8_out, not_9_out, not_10_out;
  wire [7:0] controlled_buffer_2_out;

  not not_1 (not_1_out, STP);
  assign controlled_buffer_1_out = not_1_out ? Clock : 1'bz;  // Controlled_Buffer controlled_buffer_1
  not not_2 (not_2_out, controlled_buffer_2_out[0]);
  T_Flip_Flop n0 (
    .clk(controlled_buffer_1_out), .T(1'b1), .Q(out_5[0]), .Qn(n0_qn), .preset(controlled_buffer_2_out[0]),
    .reset(not_2_out));  // open: en
  not not_3 (not_3_out, Clock);
  T_Flip_Flop n1 (
    .clk(n0_qn), .T(1'b1), .Q(out_5[1]), .Qn(n1_qn), .preset(controlled_buffer_2_out[1]), .reset(not_4_out));  // open: en
  not not_4 (not_4_out, controlled_buffer_2_out[1]);
  assign controlled_buffer_2_out = and_1_out ? JMPAdress : 8'bz;  // Controlled_Buffer controlled_buffer_2
  and and_1 (and_1_out, not_3_out, JMP);
  T_Flip_Flop n2 (
    .clk(n1_qn), .T(1'b1), .Q(out_5[2]), .Qn(n2_qn), .preset(controlled_buffer_2_out[2]), .reset(not_5_out));  // open: en
  not not_5 (not_5_out, controlled_buffer_2_out[2]);
  T_Flip_Flop n3 (
    .clk(n2_qn), .T(1'b1), .Q(out_5[3]), .Qn(n3_qn), .preset(controlled_buffer_2_out[3]), .reset(not_6_out));  // open: en
  not not_6 (not_6_out, controlled_buffer_2_out[3]);
  not not_7 (not_7_out, controlled_buffer_2_out[4]);
  T_Flip_Flop n4 (
    .clk(n3_qn), .T(1'b1), .Q(out_5[4]), .Qn(n4_qn), .preset(controlled_buffer_2_out[4]), .reset(not_7_out));  // open: en
  T_Flip_Flop n5 (
    .clk(n4_qn), .T(1'b1), .Q(out_5[5]), .Qn(n5_qn), .preset(controlled_buffer_2_out[5]), .reset(not_8_out));  // open: en
  not not_8 (not_8_out, controlled_buffer_2_out[5]);
  T_Flip_Flop n6 (
    .clk(n5_qn), .T(1'b1), .Q(out_5[6]), .Qn(n6_qn), .preset(controlled_buffer_2_out[6]), .reset(not_9_out));  // open: en
  not not_9 (not_9_out, controlled_buffer_2_out[6]);
  T_Flip_Flop n7 (
    .clk(n6_qn), .T(1'b1), .Q(out_5[7]), .preset(controlled_buffer_2_out[7]), .reset(not_10_out));  // open: Qn, en
  not not_10 (not_10_out, controlled_buffer_2_out[7]);
endmodule

module CTRL (
  input  [7:0] Instruction,
  input  Clock,
  output CtrlRam,
  output CtrlStr,
  output CtrlAcc,
  output CtrlJmp,
  output CtrlStp
);

  wire nor_1_out;

  Identifica_Comando Idenfica_Comando (
    .\Instrução (Instruction), .LDA(CtrlAcc), .STA(CtrlStr), .JMP(CtrlJmp), .STP(CtrlStp));  // open: NOP
  nor nor_1 (nor_1_out, CtrlAcc, CtrlStr);
  or or_1 (CtrlRam, nor_1_out, Clock);
endmodule

module Identifica_Comando (
  input  [7:0] \Instrução ,
  output LDA,
  output STA,
  output NOP,
  output JMP,
  output STP
);

  Comparator comparator_1 (.a(\Instrução ), .b(8'hb), .eq(LDA));  // open: gt, lt
  Comparator comparator_2 (.a(\Instrução ), .b(8'hc), .eq(STA));  // open: gt, lt
  Comparator comparator_3 (.a(\Instrução ), .b(8'h32), .eq(NOP));  // open: gt, lt
  Comparator comparator_4 (.a(\Instrução ), .b(8'h33), .eq(JMP));  // open: gt, lt
  Comparator comparator_5 (.a(\Instrução ), .b(8'h46), .eq(STP));  // open: gt, lt
endmodule

module Divisor16to8 (
  input  [15:0] in_1,
  output [7:0] Parameter,
  output [7:0] Parameter_2,
  output [7:0] Instruction
);


  assign Instruction = in_1[15:8];
  assign Parameter = in_1[7:0];
  assign Parameter_2 = in_1[7:0];
endmodule

module IR (
  input  [15:0] in_1,
  input  Clock,
  output [7:0] Parameter,
  output [7:0] Parameter_2,
  output [7:0] Instruction
);

  wire [15:0] NucleoIR_q;

  Register #(.width(16), .trigger("high")) NucleoIR (.D(in_1), .Q(NucleoIR_q), .clk(Clock));  // open: en, clr
  Divisor16to8 Divisor16to8 (
    .in_1(NucleoIR_q), .Parameter(Parameter), .Parameter_2(Parameter_2), .Instruction(Instruction));
endmodule

module RAM (
  input  [7:0] in_1,
  input  [7:0] in_2,
  input  [15:0] in_3,
  input  CtrlStr,
  input  Clock,
  input  CtrlRam,
  output [15:0] \Saída_RAM 
);

  wire and_1_out, clock_1_out;
  wire [7:0] multiplexer_1_out;

  Clock clock_1 (.out(clock_1_out));
  and and_1 (and_1_out, clock_1_out, CtrlRam);
  Multiplexer #(.width(8), .enable("false")) multiplexer_1 (
    .in0(in_1), .in1(in_2), .out(multiplexer_1_out), .sel(and_1_out));
  RAM_part #(.dataWidth(16), .bus("separate")) ram_1 (
    .addr(multiplexer_1_out), .din(in_3), .data(\Saída_RAM ), .str(CtrlStr), .clk(Clock), .ld(1'b1));  // open: sel, clr
endmodule
